# Fritzing sketch GameBloke (saved by Fritzing 0.9.3b)

parts:
  Teensy1 = Teensy 3.6 (Basic)
  J1 = female pin header, 20 pins [form="♀ (female)"]
  J2 = female pin header, 20 pins [form="♀ (female)"]
  LED1 = RGB LED (com. cathode, rbg) [package="5 mm [THT]"]
  R1 = Resistor [tolerance=±5% resistance=220 package=THT]
  R2 = Resistor [tolerance=±5% resistance=220 package=THT]
  R3 = Resistor [tolerance=±5% resistance=220 package=THT]
  R4 = Resistor [tolerance=±5% resistance=47 package=THT]
  S10 = Pushbutton [package="[SMD]"]
  S17 = Pushbutton [package="[THT]"]
  S2 = Pushbutton [package="[THT]"]
  S3 = Pushbutton [package="[THT]"]
  S14 = Pushbutton [package="[THT]"]
  S16 = Pushbutton [package="[THT]"]
  S13 = Pushbutton [package="[THT]"]
  S15 = Pushbutton [package="[THT]"]
  S4 = Pushbutton [package="[THT]"]
  S5 = Pushbutton [package="[THT]"]
  S6 = Pushbutton [package="[THT]"]
  S7 = Pushbutton [package="[THT]"]
  S8 = Pushbutton [package="[THT]"]
  S9 = Pushbutton [package="[THT]"]
  S11 = Pushbutton [package="[THT]"]
  S12 = Pushbutton [package="[THT]"]
  J3 = male pin header, 4 pins [form="♂ (male)"]
  C1 = Electrolytic Capacitor [capacitance=0.1mF package="100 mil [THT, electrolytic]"]

nets:
  N1: Teensy1.GND, J1.pin1, S17.Pin_3, S17.Pin_4, J3.pin1
  N2: Teensy1.D2, J1.pin7
  N3: Teensy1.D5, J1.pin14
  N4: Teensy1.D6, J1.pin11
  N5: Teensy1.D7, J1.pin9
  N6: Teensy1.D8, J1.pin10
  N7: Teensy1.D9, J2.pin4
  N8: Teensy1.D10, J2.pin5
  N9: Teensy1.D11, J2.pin7
  N10: Teensy1.D12, J2.pin8
  N11: Teensy1.D13, J2.pin6
  N12: Teensy1.A0/D14, J1.pin8
  N13: Teensy1.A1/D15, J2.pin1
  N14: Teensy1.A2/D16, J1.pin4
  N15: Teensy1.A3/D17, J1.pin5
  N16: Teensy1.A4/D18, J1.pin15
  N17: Teensy1.A5/D19, J1.pin17
  N18: Teensy1.A6/D20, J1.pin12
  N19: Teensy1.A7/D21, J1.pin13
  N20: Teensy1.A8/D22, J2.pin2
  N21: Teensy1.A9/D23, J2.pin3
  N22: Teensy1.3V3, LED1.common_cathode
  N23: Teensy1.Vin, J1.pin2, J1.pin6, R4.Pin_0, J3.pin4, C1.+
  N24: Teensy1.D24, S3.Pin_4, S14.Pin_1, S14.Pin_2, S16.Pin_2, S13.Pin_1, S13.Pin_2, S15.Pin_1, S15.Pin_2
  N25: Teensy1.D25, S10.Pin_1, S2.Pin_3, S2.Pin_4, S9.Pin_1, S11.Pin_1, S12.Pin_1, S12.Pin_2
  N26: Teensy1.D26, S4.Pin_2, S5.Pin_2, S6.Pin_2, S7.Pin_2, S8.Pin_2
  N27: Teensy1.D27, S2.Pin_1, S2.Pin_2, S3.Pin_2, S4.Pin_3, S4.Pin_4
  N28: Teensy1.D28, S13.Pin_3, S13.Pin_4, S5.Pin_3, S5.Pin_4, S9.Pin_3, S9.Pin_4
  N29: Teensy1.D29, S10.Pin_3, S10.Pin_4, S14.Pin_3, S14.Pin_4, S6.Pin_3, S6.Pin_4
  N30: Teensy1.D30, S16.Pin_3, S16.Pin_4, S7.Pin_3, S7.Pin_4, S11.Pin_3, S11.Pin_4
  N31: Teensy1.D31, S15.Pin_3, S15.Pin_4, S8.Pin_3, S8.Pin_4, S12.Pin_3, S12.Pin_4
  N32: Teensy1.D36, R1.Pin_0
  N33: Teensy1.D37, R2.Pin_0
  N34: Teensy1.D38, R3.Pin_0
  N35: Teensy1.D39, S17.Pin_1, S17.Pin_2
  N36: Teensy1.A21/DAC0, J3.pin3
  N37: J1.pin19, R4.Pin_1
  N38: LED1.red_anode, R1.Pin_1
  N39: LED1.blue_anode, R3.Pin_1
  N40: LED1.green_anode, R2.Pin_1

notes:
  Up
  Left
  Right
  Down
  Menu
  Button 1
  Button 2
  SSD1289
  TFT LCD
  SainSmart
  LM386
  Audio Amp
  100 uF

custom parts:
  Teensy 3.6 (Basic): The Teensy is a complete USB-based microcontoller development system, in a very small footprint, capable of implementing many types of projects. All programming is done via the USB port. No special programmer is needed, only a standard micro-USB cable and a PC or Macintosh with a USB port.
